# Fritzing sketch control home equipment with bluetooth app (saved by Fritzing 0.9.4)
breadboards: 1

parts:
  Composant1 = Bluetooth HC-05 Macho
  Mod1 = Raspberry Pi Pico
  KY-2 = Keyes Relay [package=THT]
  KY-4 = Keyes Relay [package=THT]
  Display1 = LCD screen 16x2 IIC [part_number=101290]
  J1 = JST-B3P-VH [part_number=JST-B3P-VH package=THT]  # not connected
  R1 = Resistor [tolerance=±5% resistance=220 package="0805 [SMD]"]
  R2 = Resistor [tolerance=±5% resistance=220 package="2010 [SMD]"]
  LED1 = smd LED [color="Red (633nm)" package="0603 [SMD]"]
  LED2 = smd LED [color="Red (633nm)" package="0603 [SMD]"]

nets:
  N1: Composant1.TXD, Mod1.pin_7
  N2: Composant1.RXD, Mod1.pin_6
  VCC: Composant1.VCC, Mod1.pin_36, KY-2.power, KY-4.power, Display1.VCC
  GND: Composant1.GND, Mod1.pin_3, Mod1.pin_8, Mod1.pin_13, Mod1.pin_18, Mod1.pin_23, Mod1.pin_28, Mod1.pin_33, Mod1.pin_38, Mod1.pin_42, KY-2.ground, KY-4.ground, Display1.GND, R2.Pin_1
  N3: Mod1.pin_1, Display1.SCL
  N4: Mod1.pin_4, LED2.anode
  N5: Mod1.pin_5, LED1.cathode
  N6: Mod1.pin_9, KY-4.signal
  N7: Mod1.pin_10, KY-2.signal
  N8: R1.Pin_0, LED2.cathode
  N9: R2.Pin_0, LED1.anode

custom parts:
  Raspberry Pi Pico: Raspberry Pi Pico. Based around the RP2040 microcontroller the Pico is a low cost microcontroller device bringing Raspberry Pi quality, cost, and easy of use to the microcontroller space. Jan 2021, Split part in to two versions: tht (this one) and SMD. This one will drill holes for a .1 in header in pcb to allow plugging in the module as well as providing pads to solder the module to the top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
  Keyes Relay: The Keyes 5V relay module is suitable for SCM development, home appliance control. It uses a 5V~12V TIL control signal which can control DC / AC signal.
  LCD screen 16x2 IIC: LCD screen with HD44780 controller enables showing text, symbols, value or anything else that comes from Croduino/Arduino. It is capable of showing 16 symbols in two lines and therefore can be used in many projects that need to send clearly visible and legible output information.. • Color of symbols: White • Backlight: Blue • Dimensions: 80 x 36 x 12 mm • Screen dimensions: 64.5 x 16 mm •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
